# Fritzing sketch Final Schematic (saved by Fritzing 0.9.9b)
breadboards: 3

parts:
  Part1 = Arduino Uno (Rev3)
  Part2 = Arduino Uno (Rev3)
  R4 = Basic Flex Resistor
  R5 = Basic Flex Resistor
  R6 = Basic Flex Resistor
  R7 = Resistor [tolerance=±5% resistance=1k package="1206 [SMD]"]
  R8 = Resistor [tolerance=±5% resistance=1k package="1206 [SMD]"]
  R9 = Resistor [tolerance=±5% resistance=1k package="1206 [SMD]"]
  R10 = Resistor [tolerance=±5% resistance=1M package="1206 [SMD]"]
  R11 = Resistor [tolerance=±5% resistance=1k package="1206 [SMD]"]
  R12 = Resistor [tolerance=±5% resistance=1M package="1206 [SMD]"]
  R13 = Resistor [tolerance=±5% resistance=1k package="1206 [SMD]"]
  R15 = Resistor [tolerance=±5% resistance=220 package="1206 [SMD]"]
  R16 = Resistor [tolerance=±5% resistance=220 package="1206 [SMD]"]
  R17 = Resistor [tolerance=±5% resistance=1k package="1206 [SMD]"]
  R18 = Photocell (LDR) [package=THT]
  LED4 = smd LED [color="Red (633nm)" package="1206 [SMD]"]
  U4 = mystery part, 3 pins [chip_label="Plant 2"]
  U5 = mystery part, 3 pins [chip_label="Plant 1"]
  U7 = mystery part, 3 pins [chip_label="RGBW LED Strip"]
  VCC1 = Battery block 9V
  C3 = Electrolytic Capacitor [capacitance=1µF voltage=35V package="1010 [SMD, electrolytic]"]
  C4 = Electrolytic Capacitor [capacitance=1µF voltage=35V package="1010 [SMD, electrolytic]"]
  R19 = Resistor [tolerance=±5% resistance=1k package="1206 [SMD]"]
  U8 = mystery part, 3 pins [chip_label="Plant 3"]
  Part3 = InvenSense MPU6050
  U9 = Vibration Motor- ROB-08449 [package=vibe-motor-10mm]
  U10 = Vibration Motor- ROB-08449 [package=vibe-motor-10mm]

nets (from the breadboard view):
  N1: Part1.A0, R15.Pin_0, R18.pin_1
  N2: Part1.A2, R11.Pin_1, C4.+
  N3: Part1.A3, R13.Pin_1, C3.+
  N4: Part1.D9_PWM, LED4.anode
  GND: Part1.GND, Part2.GND, R4.Pin_2, R5.Pin_2, R6.Pin_2, R15.Pin_1, R16.Pin_0, U7.pin3, VCC1.-, C3.-, C4.-, R19.Pin_1, Part3.GND, U9.+, U10.+
  N5: Part1.A4/SDA, Part3.SDA
  N6: Part1.A5/SCL, Part3.SCL
  N7: Part1.D5_PWM, R17.Pin_0
  N8: Part1.D6_PWM, Part2.D7
  N9: Part1.D7, Part2.D6_PWM
  5V: Part1.5V, R10.Pin_0, R12.Pin_0, R18.pin_0, Part3.VCC
  N10: Part2.A0, R4.pin_1, R7.Pin_0
  N11: Part2.A1, R5.pin_1, R8.Pin_0
  N12: Part2.A2, R6.pin_1, R9.Pin_0
  N13: Part2.D10_PWM/SS, U10.-
  N14: Part2.D11_PWM/MOSI, U9.-
  N15: Part2.5V, R7.Pin_1, R8.Pin_1, R9.Pin_1
  N16: R10.Pin_1, R11.Pin_0, U5.pin1
  N17: R12.Pin_1, R13.Pin_0, U4.pin1
  N18: R16.Pin_1, LED4.cathode
  N19: R17.Pin_1, U7.pin2
  N20: U7.pin1, VCC1.+
  N21: R19.Pin_0, U8.pin1
