# Fritzing sketch Schematic Draft1 Overcomplicated (saved by Fritzing 0.9.9b)
breadboards: 3

parts:
  Part1 = Arduino Uno (Rev3)
  Part2 = Arduino Uno (Rev3)
  Q1 = NPN-Transistor [package="SOT-23 [SMD]"]
  Q2 = NPN-Transistor [package="SOT-23 [SMD]"]
  Q3 = NPN-Transistor [package="SOT-23 [SMD]"]
  LED1 = LED - 5mm [color="Green (555nm)" current=0.030 package="5 mm [THT]"]
  LED2 = LED - 5mm [color="Green (555nm)" current=0.030 package="5 mm [THT]"]
  LED3 = LED - 5mm [color="Green (555nm)" current=0.030 package="5 mm [THT]"]
  U1 = Vibration Motor- ROB-08449 [package=vibe-motor-10mm]
  U2 = Vibration Motor- ROB-08449 [package=vibe-motor-10mm]
  U3 = Vibration Motor- ROB-08449 [package=vibe-motor-10mm]
  R1 = Resistor [tolerance=±5% power=0.25 resistance=220 package=THT]
  R2 = Resistor [tolerance=±5% power=0.25 resistance=220 package=THT]
  R3 = Resistor [tolerance=±5% power=0.25 resistance=220 package=THT]
  R4 = Basic Flex Resistor
  R5 = Basic Flex Resistor
  R6 = Basic Flex Resistor
  R7 = Resistor [tolerance=±5% resistance=1k package="1206 [SMD]"]
  R8 = Resistor [tolerance=±5% resistance=1k package="1206 [SMD]"]
  R9 = Resistor [tolerance=±5% resistance=1k package="1206 [SMD]"]
  R10 = Resistor [tolerance=±5% resistance=1M package="1206 [SMD]"]
  R11 = Resistor [tolerance=±5% resistance=1k package="1206 [SMD]"]
  R12 = Resistor [tolerance=±5% resistance=1M package="1206 [SMD]"]
  R13 = Resistor [tolerance=±5% resistance=1k package="1206 [SMD]"]
  R14 = Resistor [tolerance=±5% resistance=1k package="1206 [SMD]"]
  R15 = Resistor [tolerance=±5% resistance=220 package="1206 [SMD]"]
  R16 = Resistor [tolerance=±5% resistance=220 package="1206 [SMD]"]
  R17 = Resistor [tolerance=±5% resistance=1k package="1206 [SMD]"]
  R18 = Photocell (LDR) [package=THT]
  LED4 = smd LED [color="Red (633nm)" package="1206 [SMD]"]
  U4 = mystery part, 3 pins [chip_label="Plant 2"]
  U5 = mystery part, 3 pins [chip_label="Plant 1"]
  U6 = mystery part, 3 pins [chip_label="Plant 3"]
  U7 = mystery part, 3 pins [chip_label="RGBW LED Strip"]
  VCC1 = Battery block 9V
  C3 = Electrolytic Capacitor [capacitance=1µF voltage=35V package="1010 [SMD, electrolytic]"]
  C4 = Electrolytic Capacitor [capacitance=1µF voltage=35V package="1010 [SMD, electrolytic]"]

nets (from the schematic view):
  N1: Part1.A0, R14.Pin_1, R15.Pin_0, R16.Pin_0, U7.pin3, VCC1.-
  N2: Part1.A2, R11.Pin_1, C4.+
  N3: Part1.A3, R13.Pin_1, C3.+
  N4: Part1.D9_PWM, LED4.anode
  GND: Part1.GND, Part2.GND, Q1.1, Q2.1, Q3.1, R5.Pin_2, R6.Pin_2
  N5: Part1.D5_PWM, R17.Pin_0
  N6: Part1.D6_PWM, Part2.D7
  N7: Part1.D7, Part2.D6_PWM
  N8: Part1.5V, R10.Pin_0, R12.Pin_0, R18.pin_0
  N9: Part2.A0, R4.pin_1, R7.Pin_0
  N10: Part2.A1, R5.pin_1, R8.Pin_0
  N11: Part2.A2, R6.pin_1, R9.Pin_0
  N12: Part2.D9_PWM, Q3.0
  N13: Part2.D10_PWM/SS, Q2.0
  N14: Part2.D11_PWM/MOSI, Q1.0
  N15: Part2.5V, U1.-, U2.-, U3.-, R1.Pin_1, R2.Pin_1, R3.Pin_1, R7.Pin_1, R8.Pin_1, R9.Pin_1
  N16: LED1.cathode, U1.+
  N17: LED1.anode, R1.Pin_0
  N18: LED2.cathode, U2.+
  N19: LED2.anode, R2.Pin_0
  N20: LED3.cathode, U3.+
  N21: LED3.anode, R3.Pin_0
  N22: R10.Pin_1, R11.Pin_0, U5.pin1
  N23: R12.Pin_1, R13.Pin_0, U4.pin1
  N24: R14.Pin_0, U6.pin1, C3.-, C4.-
  N25: R15.Pin_1, R18.pin_1
  N26: R16.Pin_1, LED4.cathode
  N27: R17.Pin_1, U7.pin2
  N28: U7.pin1, VCC1.+
